// Logisim project barrel_shifter.circ as structural Verilog: 2 circuits, main circuit barrel_shifter_16
module barrel_shifter_8 (
  input  left,
  input  [7:0] d_in,
  input  [2:0] shift,
  output [7:0] d_out
);

  wire multiplexer_2_out, multiplexer_3_out, multiplexer_4_out, multiplexer_5_out, multiplexer_6_out,
       multiplexer_7_out, multiplexer_8_out, multiplexer_9_out, multiplexer_10_out, multiplexer_11_out,
       multiplexer_12_out, multiplexer_13_out, multiplexer_14_out, multiplexer_15_out, multiplexer_16_out,
       multiplexer_17_out;
  wire [7:0] multiplexer_1_out, multiplexer_25_out;

  Multiplexer #(.width(8)) multiplexer_1 (
    .in0(d_in), .in1({d_in[0], d_in[1], d_in[2], d_in[3], d_in[4], d_in[5], d_in[6], d_in[7]}),
    .out(multiplexer_1_out), .sel(left));
  Multiplexer multiplexer_2 (
    .in0(multiplexer_1_out[0]), .in1(multiplexer_1_out[1]), .out(multiplexer_2_out), .sel(shift[0]));
  Multiplexer multiplexer_3 (
    .in0(multiplexer_1_out[1]), .in1(multiplexer_1_out[2]), .out(multiplexer_3_out), .sel(shift[0]));
  Multiplexer multiplexer_4 (
    .in0(multiplexer_1_out[2]), .in1(multiplexer_1_out[3]), .out(multiplexer_4_out), .sel(shift[0]));
  Multiplexer multiplexer_5 (
    .in0(multiplexer_1_out[3]), .in1(multiplexer_1_out[4]), .out(multiplexer_5_out), .sel(shift[0]));
  Multiplexer multiplexer_6 (
    .in0(multiplexer_1_out[4]), .in1(multiplexer_1_out[5]), .out(multiplexer_6_out), .sel(shift[0]));
  Multiplexer multiplexer_7 (
    .in0(multiplexer_1_out[5]), .in1(multiplexer_1_out[6]), .out(multiplexer_7_out), .sel(shift[0]));
  Multiplexer multiplexer_8 (
    .in0(multiplexer_1_out[6]), .in1(multiplexer_1_out[7]), .out(multiplexer_8_out), .sel(shift[0]));
  Multiplexer multiplexer_9 (.in0(multiplexer_1_out[7]), .in1(1'b0), .out(multiplexer_9_out), .sel(shift[0]));
  Multiplexer multiplexer_10 (
    .in0(multiplexer_2_out), .in1(multiplexer_4_out), .out(multiplexer_10_out), .sel(shift[1]));
  Multiplexer multiplexer_11 (
    .in0(multiplexer_3_out), .in1(multiplexer_5_out), .out(multiplexer_11_out), .sel(shift[1]));
  Multiplexer multiplexer_12 (
    .in0(multiplexer_4_out), .in1(multiplexer_6_out), .out(multiplexer_12_out), .sel(shift[1]));
  Multiplexer multiplexer_13 (
    .in0(multiplexer_5_out), .in1(multiplexer_7_out), .out(multiplexer_13_out), .sel(shift[1]));
  Multiplexer multiplexer_14 (
    .in0(multiplexer_6_out), .in1(multiplexer_8_out), .out(multiplexer_14_out), .sel(shift[1]));
  Multiplexer multiplexer_15 (
    .in0(multiplexer_7_out), .in1(multiplexer_9_out), .out(multiplexer_15_out), .sel(shift[1]));
  Multiplexer multiplexer_16 (.in0(multiplexer_8_out), .in1(1'b0), .out(multiplexer_16_out), .sel(shift[1]));
  Multiplexer multiplexer_17 (.in0(multiplexer_9_out), .in1(1'b0), .out(multiplexer_17_out), .sel(shift[1]));
  Multiplexer multiplexer_18 (
    .in0(multiplexer_10_out), .in1(multiplexer_14_out), .out(multiplexer_25_out[0]), .sel(shift[2]));
  Multiplexer multiplexer_19 (
    .in0(multiplexer_11_out), .in1(multiplexer_15_out), .out(multiplexer_25_out[1]), .sel(shift[2]));
  Multiplexer multiplexer_20 (
    .in0(multiplexer_12_out), .in1(multiplexer_16_out), .out(multiplexer_25_out[2]), .sel(shift[2]));
  Multiplexer multiplexer_21 (
    .in0(multiplexer_13_out), .in1(multiplexer_17_out), .out(multiplexer_25_out[3]), .sel(shift[2]));
  Multiplexer multiplexer_22 (.in0(multiplexer_14_out), .in1(1'b0), .out(multiplexer_25_out[4]), .sel(shift[2]));
  Multiplexer multiplexer_23 (.in0(multiplexer_15_out), .in1(1'b0), .out(multiplexer_25_out[5]), .sel(shift[2]));
  Multiplexer multiplexer_24 (.in0(multiplexer_16_out), .in1(1'b0), .out(multiplexer_25_out[6]), .sel(shift[2]));
  Multiplexer multiplexer_25 (.in0(multiplexer_17_out), .in1(1'b0), .out(multiplexer_25_out[7]), .sel(shift[2]));
  Multiplexer #(.width(8)) multiplexer_26 (
    .in0(multiplexer_25_out),
    .in1({multiplexer_25_out[0], multiplexer_25_out[1], multiplexer_25_out[2], multiplexer_25_out[3], multiplexer_25_out[4], multiplexer_25_out[5], multiplexer_25_out[6], multiplexer_25_out[7]}),
    .out(d_out), .sel(left));

  // Notes on the sheet:
  //   8-bit Barrel Shifter
endmodule

module barrel_shifter_16 (
  input  left,
  input  [15:0] d_in,
  input  [3:0] shift,
  output [15:0] d_out
);

  wire multiplexer_2_out, multiplexer_3_out, multiplexer_4_out, multiplexer_5_out, multiplexer_6_out,
       multiplexer_7_out, multiplexer_8_out, multiplexer_9_out, multiplexer_10_out, multiplexer_11_out,
       multiplexer_12_out, multiplexer_13_out, multiplexer_14_out, multiplexer_15_out, multiplexer_16_out,
       multiplexer_17_out, multiplexer_18_out, multiplexer_19_out, multiplexer_20_out, multiplexer_21_out,
       multiplexer_22_out, multiplexer_23_out, multiplexer_24_out, multiplexer_25_out, multiplexer_26_out,
       multiplexer_27_out, multiplexer_28_out, multiplexer_29_out, multiplexer_30_out, multiplexer_31_out,
       multiplexer_32_out, multiplexer_33_out, multiplexer_34_out, multiplexer_35_out, multiplexer_36_out,
       multiplexer_37_out, multiplexer_38_out, multiplexer_39_out, multiplexer_40_out, multiplexer_41_out,
       multiplexer_42_out, multiplexer_43_out, multiplexer_44_out, multiplexer_45_out, multiplexer_46_out,
       multiplexer_47_out, multiplexer_48_out, multiplexer_49_out;
  wire [15:0] multiplexer_1_out, multiplexer_65_out;

  Multiplexer #(.width(16)) multiplexer_1 (
    .in0(d_in),
    .in1({d_in[0], d_in[1], d_in[2], d_in[3], d_in[4], d_in[5], d_in[6], d_in[7], d_in[8], d_in[9], d_in[10], d_in[11], d_in[12], d_in[13], d_in[14], d_in[15]}),
    .out(multiplexer_1_out), .sel(left));
  Multiplexer multiplexer_2 (
    .in0(multiplexer_1_out[0]), .in1(multiplexer_1_out[1]), .out(multiplexer_2_out), .sel(shift[0]));
  Multiplexer multiplexer_3 (
    .in0(multiplexer_1_out[1]), .in1(multiplexer_1_out[2]), .out(multiplexer_3_out), .sel(shift[0]));
  Multiplexer multiplexer_4 (
    .in0(multiplexer_1_out[2]), .in1(multiplexer_1_out[3]), .out(multiplexer_4_out), .sel(shift[0]));
  Multiplexer multiplexer_5 (
    .in0(multiplexer_1_out[3]), .in1(multiplexer_1_out[4]), .out(multiplexer_5_out), .sel(shift[0]));
  Multiplexer multiplexer_6 (
    .in0(multiplexer_1_out[4]), .in1(multiplexer_1_out[5]), .out(multiplexer_6_out), .sel(shift[0]));
  Multiplexer multiplexer_7 (
    .in0(multiplexer_1_out[5]), .in1(multiplexer_1_out[6]), .out(multiplexer_7_out), .sel(shift[0]));
  Multiplexer multiplexer_8 (
    .in0(multiplexer_1_out[6]), .in1(multiplexer_1_out[7]), .out(multiplexer_8_out), .sel(shift[0]));
  Multiplexer multiplexer_9 (
    .in0(multiplexer_1_out[7]), .in1(multiplexer_1_out[8]), .out(multiplexer_9_out), .sel(shift[0]));
  Multiplexer multiplexer_10 (
    .in0(multiplexer_1_out[8]), .in1(multiplexer_1_out[9]), .out(multiplexer_10_out), .sel(shift[0]));
  Multiplexer multiplexer_11 (
    .in0(multiplexer_1_out[9]), .in1(multiplexer_1_out[10]), .out(multiplexer_11_out), .sel(shift[0]));
  Multiplexer multiplexer_12 (
    .in0(multiplexer_1_out[10]), .in1(multiplexer_1_out[11]), .out(multiplexer_12_out), .sel(shift[0]));
  Multiplexer multiplexer_13 (
    .in0(multiplexer_1_out[11]), .in1(multiplexer_1_out[12]), .out(multiplexer_13_out), .sel(shift[0]));
  Multiplexer multiplexer_14 (
    .in0(multiplexer_1_out[12]), .in1(multiplexer_1_out[13]), .out(multiplexer_14_out), .sel(shift[0]));
  Multiplexer multiplexer_15 (
    .in0(multiplexer_1_out[13]), .in1(multiplexer_1_out[14]), .out(multiplexer_15_out), .sel(shift[0]));
  Multiplexer multiplexer_16 (
    .in0(multiplexer_1_out[14]), .in1(multiplexer_1_out[15]), .out(multiplexer_16_out), .sel(shift[0]));
  Multiplexer multiplexer_17 (.in0(multiplexer_1_out[15]), .in1(1'b0), .out(multiplexer_17_out), .sel(shift[0]));
  Multiplexer multiplexer_18 (
    .in0(multiplexer_2_out), .in1(multiplexer_4_out), .out(multiplexer_18_out), .sel(shift[1]));
  Multiplexer multiplexer_19 (
    .in0(multiplexer_3_out), .in1(multiplexer_5_out), .out(multiplexer_19_out), .sel(shift[1]));
  Multiplexer multiplexer_20 (
    .in0(multiplexer_4_out), .in1(multiplexer_6_out), .out(multiplexer_20_out), .sel(shift[1]));
  Multiplexer multiplexer_21 (
    .in0(multiplexer_5_out), .in1(multiplexer_7_out), .out(multiplexer_21_out), .sel(shift[1]));
  Multiplexer multiplexer_22 (
    .in0(multiplexer_6_out), .in1(multiplexer_8_out), .out(multiplexer_22_out), .sel(shift[1]));
  Multiplexer multiplexer_23 (
    .in0(multiplexer_7_out), .in1(multiplexer_9_out), .out(multiplexer_23_out), .sel(shift[1]));
  Multiplexer multiplexer_24 (
    .in0(multiplexer_8_out), .in1(multiplexer_10_out), .out(multiplexer_24_out), .sel(shift[1]));
  Multiplexer multiplexer_25 (
    .in0(multiplexer_9_out), .in1(multiplexer_11_out), .out(multiplexer_25_out), .sel(shift[1]));
  Multiplexer multiplexer_26 (
    .in0(multiplexer_10_out), .in1(multiplexer_12_out), .out(multiplexer_26_out), .sel(shift[1]));
  Multiplexer multiplexer_27 (
    .in0(multiplexer_11_out), .in1(multiplexer_13_out), .out(multiplexer_27_out), .sel(shift[1]));
  Multiplexer multiplexer_28 (
    .in0(multiplexer_12_out), .in1(multiplexer_14_out), .out(multiplexer_28_out), .sel(shift[1]));
  Multiplexer multiplexer_29 (
    .in0(multiplexer_13_out), .in1(multiplexer_15_out), .out(multiplexer_29_out), .sel(shift[1]));
  Multiplexer multiplexer_30 (
    .in0(multiplexer_14_out), .in1(multiplexer_16_out), .out(multiplexer_30_out), .sel(shift[1]));
  Multiplexer multiplexer_31 (
    .in0(multiplexer_15_out), .in1(multiplexer_17_out), .out(multiplexer_31_out), .sel(shift[1]));
  Multiplexer multiplexer_32 (.in0(multiplexer_16_out), .in1(1'b0), .out(multiplexer_32_out), .sel(shift[1]));
  Multiplexer multiplexer_33 (.in0(multiplexer_17_out), .in1(1'b0), .out(multiplexer_33_out), .sel(shift[1]));
  Multiplexer multiplexer_34 (
    .in0(multiplexer_18_out), .in1(multiplexer_22_out), .out(multiplexer_34_out), .sel(shift[2]));
  Multiplexer multiplexer_35 (
    .in0(multiplexer_19_out), .in1(multiplexer_23_out), .out(multiplexer_35_out), .sel(shift[2]));
  Multiplexer multiplexer_36 (
    .in0(multiplexer_20_out), .in1(multiplexer_24_out), .out(multiplexer_36_out), .sel(shift[2]));
  Multiplexer multiplexer_37 (
    .in0(multiplexer_21_out), .in1(multiplexer_25_out), .out(multiplexer_37_out), .sel(shift[2]));
  Multiplexer multiplexer_38 (
    .in0(multiplexer_22_out), .in1(multiplexer_26_out), .out(multiplexer_38_out), .sel(shift[2]));
  Multiplexer multiplexer_39 (
    .in0(multiplexer_23_out), .in1(multiplexer_27_out), .out(multiplexer_39_out), .sel(shift[2]));
  Multiplexer multiplexer_40 (
    .in0(multiplexer_24_out), .in1(multiplexer_28_out), .out(multiplexer_40_out), .sel(shift[2]));
  Multiplexer multiplexer_41 (
    .in0(multiplexer_25_out), .in1(multiplexer_29_out), .out(multiplexer_41_out), .sel(shift[2]));
  Multiplexer multiplexer_42 (
    .in0(multiplexer_26_out), .in1(multiplexer_30_out), .out(multiplexer_42_out), .sel(shift[2]));
  Multiplexer multiplexer_43 (
    .in0(multiplexer_27_out), .in1(multiplexer_31_out), .out(multiplexer_43_out), .sel(shift[2]));
  Multiplexer multiplexer_44 (
    .in0(multiplexer_28_out), .in1(multiplexer_32_out), .out(multiplexer_44_out), .sel(shift[2]));
  Multiplexer multiplexer_45 (
    .in0(multiplexer_29_out), .in1(multiplexer_33_out), .out(multiplexer_45_out), .sel(shift[2]));
  Multiplexer multiplexer_46 (.in0(multiplexer_30_out), .in1(1'b0), .out(multiplexer_46_out), .sel(shift[2]));
  Multiplexer multiplexer_47 (.in0(multiplexer_31_out), .in1(1'b0), .out(multiplexer_47_out), .sel(shift[2]));
  Multiplexer multiplexer_48 (.in0(multiplexer_32_out), .in1(1'b0), .out(multiplexer_48_out), .sel(shift[2]));
  Multiplexer multiplexer_49 (.in0(multiplexer_33_out), .in1(1'b0), .out(multiplexer_49_out), .sel(shift[2]));
  Multiplexer multiplexer_50 (
    .in0(multiplexer_34_out), .in1(multiplexer_39_out), .out(multiplexer_65_out[0]), .sel(shift[3]));
  Multiplexer multiplexer_51 (
    .in0(multiplexer_35_out), .in1(multiplexer_40_out), .out(multiplexer_65_out[1]), .sel(shift[3]));
  Multiplexer multiplexer_52 (
    .in0(multiplexer_36_out), .in1(multiplexer_41_out), .out(multiplexer_65_out[2]), .sel(shift[3]));
  Multiplexer multiplexer_53 (
    .in0(multiplexer_37_out), .in1(multiplexer_42_out), .out(multiplexer_65_out[3]), .sel(shift[3]));
  Multiplexer multiplexer_54 (
    .in0(multiplexer_38_out), .in1(multiplexer_43_out), .out(multiplexer_65_out[4]), .sel(shift[3]));
  Multiplexer multiplexer_55 (
    .in0(multiplexer_39_out), .in1(multiplexer_44_out), .out(multiplexer_65_out[5]), .sel(shift[3]));
  Multiplexer multiplexer_56 (
    .in0(multiplexer_40_out), .in1(multiplexer_45_out), .out(multiplexer_65_out[6]), .sel(shift[3]));
  Multiplexer multiplexer_57 (
    .in0(multiplexer_41_out), .in1(multiplexer_46_out), .out(multiplexer_65_out[7]), .sel(shift[3]));
  Multiplexer multiplexer_58 (.in0(multiplexer_42_out), .in1(1'b0), .out(multiplexer_65_out[8]), .sel(shift[3]));
  Multiplexer multiplexer_59 (.in0(multiplexer_43_out), .in1(1'b0), .out(multiplexer_65_out[9]), .sel(shift[3]));
  Multiplexer multiplexer_60 (.in0(multiplexer_44_out), .in1(1'b0), .out(multiplexer_65_out[10]), .sel(shift[3]));
  Multiplexer multiplexer_61 (.in0(multiplexer_45_out), .in1(1'b0), .out(multiplexer_65_out[11]), .sel(shift[3]));
  Multiplexer multiplexer_62 (.in0(multiplexer_46_out), .in1(1'b0), .out(multiplexer_65_out[12]), .sel(shift[3]));
  Multiplexer multiplexer_63 (.in0(multiplexer_47_out), .in1(1'b0), .out(multiplexer_65_out[13]), .sel(shift[3]));
  Multiplexer multiplexer_64 (.in0(multiplexer_48_out), .in1(1'b0), .out(multiplexer_65_out[14]), .sel(shift[3]));
  Multiplexer multiplexer_65 (.in0(multiplexer_49_out), .in1(1'b0), .out(multiplexer_65_out[15]), .sel(shift[3]));
  Multiplexer #(.width(16)) multiplexer_66 (
    .in0(multiplexer_65_out),
    .in1({multiplexer_65_out[0], multiplexer_65_out[1], multiplexer_65_out[2], multiplexer_65_out[3], multiplexer_65_out[4], multiplexer_65_out[5], multiplexer_65_out[6], multiplexer_65_out[7], multiplexer_65_out[8], multiplexer_65_out[9], multiplexer_65_out[10], multiplexer_65_out[11], multiplexer_65_out[12], multiplexer_65_out[13], multiplexer_65_out[14], multiplexer_65_out[15]}),
    .out(d_out), .sel(left));

  // Notes on the sheet:
  //   16-bit Barrel Shifter
endmodule
